# Fritzing sketch end_device_class_c (saved by Fritzing 1.0.2b)

parts:
  M1 = prefix0000
  Mod1 = Heltec WiFi LoRa 32 V2 [part_number=HTIT-WB32LA]
  LED1 = LED - 5mm [color="Red (633nm)" current=0.030A package="5 mm [THT]"]

nets:
  N1: M1.connector0, Mod1.pin_20
  N2: M1.connector1, Mod1.GND, LED1.cathode
  N3: M1.connector2, Mod1.pin_27
  N4: M1.connector3, Mod1.pin_1
  N5: Mod1.pin_29, LED1.anode
